# Fritzing sketch AMIS30543 (saved by Fritzing 0.9.3b)
circuit board: 4.99684cm x 4.00493cm
breadboards: 2

parts:
  VMOT/GND = female pin header, 2 pins [form="♀ (female)"]
  VD(Out)/IORef = female pin header, 2 pins [form="♀ (female)"]
  ItsyBitsy_M4 = Adafruit ItsyBitsy M4 [part_number="Adafruit #3800"]
  D1 = Rectifier Diode 10A [part_number=P1000K]
  AMIS_30543 = female pin header, 11 pins [form="♀ (female)"]
  part = female pin header, 1 pin [form="♀ (female)"]
  part_2 = female pin header, 1 pin [form="♀ (female)"]
  GND/5V+ = screw terminal, 2 pins
  Fuse = Screw terminal - 2 pins [package=THT]

nets:
  N1: VMOT/GND.pin1, Fuse.pin2
  N2: VMOT/GND.pin2, GND/5V+.pin1
  N3: VD(Out)/IORef.pin1, ItsyBitsy_M4.VHI
  N4: ItsyBitsy_M4.GND, AMIS_30543.pin11
  N5: ItsyBitsy_M4.D12, AMIS_30543.pin10
  N6: ItsyBitsy_M4.D11, AMIS_30543.pin3
  N7: ItsyBitsy_M4.D10, AMIS_30543.pin4
  N8: ItsyBitsy_M4.D9, AMIS_30543.pin5
  N9: ItsyBitsy_M4.D7, AMIS_30543.pin9
  N10: ItsyBitsy_M4.MISO, AMIS_30543.pin8
  N11: ItsyBitsy_M4.MOSI, AMIS_30543.pin7
  N12: ItsyBitsy_M4.SCK, AMIS_30543.pin6
  N13: D1.cathode, part.pin1, Fuse.pin1
  N14: D1.anode, part_2.pin1, GND/5V+.pin2

notes:
  GND
  NXT/STEP
  DIR
  DO
  DI
  CLK
  CS
  CLR
  ERR
  POR/WD
  SLA
  USB
  Stepper Driver Board V. 1.2
  W. Birkfellner 2018

custom parts:
  Adafruit ItsyBitsy M4: What's smaller than a Feather but larger than a Trinket? It's an Adafruit ItsyBitsy M4 Express featuring the Microchip ATSAMD51! Small, powerful, with a ultra fast ATSAMD51 Cortex M4 processor running at 120 MHz - this microcontroller board is perfect when you want something very compact, with a ton of horsepower and a bunch of pins. This Itsy is like a bullet train, with it's 120MHz Cortex M4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
