# Fritzing sketch ConnectorBreakout (saved by Fritzing 0.9.3b)
circuit board: 7.45038cm x 5.42696cm
breadboards: 2

parts:
  Dr_1 = RJ11 Jack [package=rj11-6]
  AA'-BB' = screw terminal, 4 pins
  Dr_2 = RJ11 Jack [package=rj11-6]
  AA'-BB'_2 = screw terminal, 4 pins
  ST4 = RJ11 Jack [package=rj11-6]
  COM/N/E/S/W = screw terminal, 5 pins
  Dr_3 = RJ11 Jack [package=rj11-6]
  Dr_4 = RJ11 Jack [package=rj11-6]
  Temp = RJ11 Jack [package=rj11-6]
  AA'-BB'1 = screw terminal, 4 pins
  AA'-BB'2 = screw terminal, 4 pins
  +/GND/- = screw terminal, 3 pins

nets:
  N1: Dr_1.2, AA'-BB'.pin1
  N2: Dr_1.3, AA'-BB'.pin2
  N3: Dr_1.4, AA'-BB'.pin3
  N4: Dr_1.5, AA'-BB'.pin4
  N5: Dr_2.2, AA'-BB'_2.pin1
  N6: Dr_2.3, AA'-BB'_2.pin2
  N7: Dr_2.4, AA'-BB'_2.pin3
  N8: Dr_2.5, AA'-BB'_2.pin4
  N9: ST4.2, COM/N/E/S/W.pin1
  N10: ST4.3, COM/N/E/S/W.pin5
  N11: ST4.4, COM/N/E/S/W.pin2
  N12: ST4.5, COM/N/E/S/W.pin3
  N13: ST4.6, COM/N/E/S/W.pin4
  N14: Dr_3.2, AA'-BB'1.pin1
  N15: Dr_3.3, AA'-BB'1.pin2
  N16: Dr_3.4, AA'-BB'1.pin3
  N17: Dr_3.5, AA'-BB'1.pin4
  N18: Dr_4.2, AA'-BB'2.pin1
  N19: Dr_4.3, AA'-BB'2.pin2
  N20: Dr_4.4, AA'-BB'2.pin3
  N21: Dr_4.5, AA'-BB'2.pin4
  N22: Temp.3, +/GND/-.pin1
  N23: Temp.4, +/GND/-.pin2
  N24: Temp.5, +/GND/-.pin3
