# Fritzing sketch TSC_PiHat_ILD (saved by Fritzing 0.9.3b)
circuit board: 8.63058cm x 6.88934cm
breadboards: 3

parts:
  DS_3231 = Adafruit DS3231 [part_number="Adafruit #3013"]
  ST_4 = RJ12
  FTDI = Adafruit FTDI Friend [part_number="Adafruit #284"]
  R2 = Resistor [tolerance=±5% resistance=4.7k package=THT]
  R3 = Resistor [tolerance=±5% resistance=4.7k package=THT]
  BC547 = TRANSISTOR_NPN [package=to-92-ammo]
  BC547_2 = TRANSISTOR_NPN [package=to-92-ammo]
  RNG = female pin header, 1 pin [form="♀ (female)"]
  TIP = female pin header, 1 pin [form="♀ (female)"]
  GND = female pin header, 1 pin [form="♀ (female)"]
  J1 = double row female pin header, 40 pins [form="♀ (female)"]
  SPI_Mo/Mi/Cl/SS0/SS1 = screw terminal, 5 pins
  R4 = Resistor [tolerance=±5% resistance=470 package=THT]
  R5 = Resistor [tolerance=±5% resistance=1k package=THT]
  ILD = IC, DIP package, 8 pins [chip_label=IC]
  R6 = Resistor [tolerance=±5% resistance=220 package=THT]
  R7 = Resistor [tolerance=±5% resistance=220 package=THT]
  ILD_2 = IC, DIP package, 8 pins [chip_label=IC]
  R8 = Resistor [tolerance=±5% resistance=220 package=THT]
  R9 = Resistor [tolerance=±5% resistance=220 package=THT]
  ILD_3 = IC, DIP package, 8 pins [chip_label=IC]
  R10 = Resistor [tolerance=±5% resistance=220 package=THT]
  R11 = Resistor [tolerance=±5% resistance=220 package=THT]
  R12 = Resistor [tolerance=±5% resistance=4.7k package=THT]
  R13 = Resistor [tolerance=±5% resistance=4.7k package=THT]
  R14 = Resistor [tolerance=±5% resistance=4.7k package=THT]
  R15 = Resistor [tolerance=±5% resistance=4.7k package=THT]

nets:
  N1: DS_3231.Vin, J1.pin1, ILD.pin5, ILD.pin8, R6.Pin_1, R7.Pin_0, ILD_2.pin5, ILD_2.pin8, R8.Pin_0, R9.Pin_1, R12.Pin_1, R13.Pin_0, R14.Pin_1, R15.Pin_0
  GND: DS_3231.GND, ST_4.pin_2, FTDI.GND, BC547.E, BC547_2.E, J1.pin5, R5.Pin_1, R12.Pin_0, R13.Pin_1, R14.Pin_0, R15.Pin_1
  N2: DS_3231.SCL, J1.pin3
  N3: DS_3231.SDA, J1.pin2
  N4: ST_4.pin_3, ILD.pin2
  N5: ST_4.pin_4, ILD_2.pin2
  N6: ST_4.pin_5, ILD_2.pin3
  N7: ST_4.pin_6, ILD.pin3
  N8: FTDI.VCC, J1.pin40, R10.Pin_0, R11.Pin_1
  N9: FTDI.TX, J1.pin36
  N10: FTDI.RX, J1.pin37
  N11: R2.Pin_0, J1.pin23
  N12: R2.Pin_1, BC547.B
  N13: R3.Pin_0, J1.pin35
  N14: R3.Pin_1, BC547_2.B
  N15: BC547.C, ILD_3.pin3
  N16: BC547_2.C, ILD_3.pin2
  N17: RNG.pin1, ILD_3.pin6
  N18: TIP.pin1, ILD_3.pin7
  N19: GND.pin1, ILD_3.pin5, ILD_3.pin8
  N20: J1.pin7, ILD.pin7
  N21: J1.pin8, ILD_2.pin7
  N22: J1.pin10, SPI_Mo/Mi/Cl/SS0/SS1.pin1
  N23: J1.pin11, R4.Pin_1, R5.Pin_0
  N24: J1.pin12, SPI_Mo/Mi/Cl/SS0/SS1.pin3
  N25: J1.pin28, SPI_Mo/Mi/Cl/SS0/SS1.pin5
  N26: J1.pin29, SPI_Mo/Mi/Cl/SS0/SS1.pin4
  N27: J1.pin32, ILD_2.pin6
  N28: J1.pin33, ILD.pin6
  N29: SPI_Mo/Mi/Cl/SS0/SS1.pin2, R4.Pin_0
  N30: ILD.pin1, R7.Pin_1
  N31: ILD.pin4, R6.Pin_0
  N32: ILD_2.pin1, R8.Pin_1
  N33: ILD_2.pin4, R9.Pin_0
  N34: ILD_3.pin1, R10.Pin_1
  N35: ILD_3.pin4, R11.Pin_0

notes:
  TSC  V1.2
  Vin
  GND
  DSLR
  W. Birkfellner/S. Elste 2017

custom parts:
  Adafruit DS3231: The datasheet for the DS3231 explains that this part is an "Extremely Accurate I²C-Integrated RTC/TCXO/Crystal". And, hey, it does exactly what it says on the tin! This Real Time Clock (RTC) is the most precise you can get in a small, low power package. Most RTCs use an external 32kHz timing crystal that is used to keep time with low current draw. And that's all well and good, but those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
  Adafruit FTDI Friend: Long gone are the days of parallel ports and serial ports. Now the USB port reigns supreme! But USB is hard, and you just want to transfer your every-day serial data from a microcontroller to computer. What now? Enter the FTDI Friend! The FTDI Friend is a tweaked out FTDI FT232RL chip adapter. Sure, like the well-known FTDI cable, it can provide power to your project and there are 4 signal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
