# Fritzing sketch TSC_PiHat_SMD_ADuM (saved by Fritzing 0.9.0b)
circuit board: 10.1205cm x 8.14338cm
breadboards: 2

parts:
  DS_3241 = Adafruit DS3231 [part_number="Adafruit #3013"]
  TRACO = female pin header, 6 pins [form="♀ (female)"]
  U1 = DIODE-ZENER [package=diode-zener]
  ST_4 = RJ12
  Pi = double row female pin header, 40 pins [form="♀ (female)"]
  R1 = Resistor [tolerance=±5% resistance=100 package=THT]
  PWR_out_(GND/3_3/5) = screw terminal, 3 pins
  FTDI = Adafruit FTDI Friend [part_number="Adafruit #284"]
  R2 = Resistor [tolerance=±5% resistance=4.7k package=THT]
  R3 = Resistor [tolerance=±5% resistance=4.7k package=THT]
  BC547 = TRANSISTOR_NPN [package=to-92-ammo]
  BC547_2 = TRANSISTOR_NPN [package=to-92-ammo]
  RNG = female pin header, 1 pin [form="♀ (female)"]
  TIP = female pin header, 1 pin [form="♀ (female)"]
  GND = female pin header, 1 pin [form="♀ (female)"]
  GPIO = female pin header, 6 pins [form="♀ (female)"]
  SPI_Mo/Mi/Cl/GND = screw terminal, 6 pins
  ADuM = SOIC18-W [chip_label=SOIC18-W package=SO(w)]

nets:
  VIN: DS_3241.Vin, Pi.pin1, FTDI.VCC
  GND: DS_3241.GND, TRACO.pin2, ST_4.pin_2, Pi.pin5, PWR_out_(GND/3_3/5).pin3, FTDI.GND, BC547.E, BC547_2.E, GND.pin1, ADuM.2, ADuM.8
  N1: DS_3241.SCL, Pi.pin3
  N2: DS_3241.SDA, Pi.pin2
  N3: TRACO.pin1, Pi.pin40, PWR_out_(GND/3_3/5).pin2, ADuM.1
  N4: TRACO.pin4, U1.A, ADuM.11, ADuM.17
  N5: TRACO.pin6, R1.Pin_1
  N6: U1.C, R1.Pin_0, ADuM.18
  N7: ST_4.pin_3, ADuM.5
  N8: ST_4.pin_4, ADuM.4
  N9: ST_4.pin_5, ADuM.3
  N10: ST_4.pin_6, ADuM.6
  N11: Pi.pin7, ADuM.16
  N12: Pi.pin8, ADuM.13
  N13: Pi.pin9, PWR_out_(GND/3_3/5).pin1
  N14: Pi.pin10, SPI_Mo/Mi/Cl/GND.pin1
  N15: Pi.pin11, SPI_Mo/Mi/Cl/GND.pin2
  N16: Pi.pin12, SPI_Mo/Mi/Cl/GND.pin3
  N17: Pi.pin13, SPI_Mo/Mi/Cl/GND.pin4
  N18: Pi.pin15, GPIO.pin1
  N19: Pi.pin16, GPIO.pin2
  N20: Pi.pin17, GPIO.pin3
  N21: Pi.pin18, GPIO.pin4
  N22: Pi.pin19, GPIO.pin5
  N23: Pi.pin20, GPIO.pin6
  N24: Pi.pin23, R2.Pin_0
  N25: Pi.pin28, SPI_Mo/Mi/Cl/GND.pin6
  N26: Pi.pin29, SPI_Mo/Mi/Cl/GND.pin5
  N27: Pi.pin32, ADuM.14
  N28: Pi.pin33, ADuM.15
  N29: Pi.pin35, R3.Pin_0
  N30: Pi.pin36, FTDI.TX
  N31: Pi.pin37, FTDI.RX
  N32: R2.Pin_1, BC547.B
  N33: R3.Pin_1, BC547_2.B
  N34: BC547.C, RNG.pin1
  N35: BC547_2.C, TIP.pin1

notes:
  TSC
  V. 1
  W. Birkfellner  2017
  Vin
  GND
  DSLR

custom parts:
  Adafruit DS3231: The datasheet for the DS3231 explains that this part is an "Extremely Accurate I²C-Integrated RTC/TCXO/Crystal". And, hey, it does exactly what it says on the tin! This Real Time Clock (RTC) is the most precise you can get in a small, low power package. Most RTCs use an external 32kHz timing crystal that is used to keep time with low current draw. And that's all well and good, but those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
  Adafruit FTDI Friend: Long gone are the days of parallel ports and serial ports. Now the USB port reigns supreme! But USB is hard, and you just want to transfer your every-day serial data from a microcontroller to computer. What now? Enter the FTDI Friend! The FTDI Friend is a tweaked out FTDI FT232RL chip adapter. Sure, like the well-known FTDI cable, it can provide power to your project and there are 4 signal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
